# Fritzing sketch Maket (saved by Fritzing 0.9.2b)

parts:
  Часть1 = Arduino Pro Mini v13
  Часть2 = Triple Axis Magnetometer - HMC5883 Breakout
  GY521 = MPU-6050 Board GY-521 [form="♀ (female)" package=THT]
  M1 = DC Motor
  U1 = L298 [package=multiwatt15]
  M2 = DC Motor
  part = DC Power [voltage=5]  # not connected
  part_2 = DC Power [voltage=12V]

nets:
  VCC: Часть1.VCC, Часть2.VCC, GY521.pin1
  N1: Часть1.A4, GY521.pin3
  N2: Часть1.A5, GY521.pin4
  GND: Часть1.GND, Часть2.GND, GY521.pin2, U1.GND, part_2.V-
  N3: Часть1.D8, U1.IN1
  N4: Часть1.D7, U1.IN2
  N5: Часть1.D6_PWM, U1.ENA
  N6: Часть1.D4, U1.IN4
  N7: Часть1.D3_PWM, U1.ENB
  N8: Часть1.D2, U1.IN3
  N9: Часть2.SDA, GY521.pin5
  N10: Часть2.SCL, GY521.pin6
  N11: M1.pin_1, U1.OUT4
  N12: M1.pin_2, U1.OUT3
  N13: U1.OUT1, M2.pin_2
  N14: U1.OUT2, M2.pin_1
  N15: U1.VS, part_2.V+

custom parts:
  MPU-6050 Board GY-521: Acelerometro y Giroscopio MPU-6050 Board GY-521
