# Fritzing sketch Untitled Sketch (saved by Fritzing 0.9.2b)

parts:
  Часть1 = Arduino Pro Mini v13
  Часть2 = Triple Axis Magnetometer - HMC5883 Breakout
  GY2 = MPU-6050 Board GY-521 [form="♀ (female)" package=THT]
  S1 = H-Bridge with L298N
  M1 = DC Motor
  M2 = DC Motor

nets:
  VCC: Часть1.VCC, Часть2.VCC, GY2.pin1
  N1: Часть1.A4, GY2.pin3
  N2: Часть1.A5, GY2.pin4
  GND: Часть1.GND, Часть2.GND, GY2.pin2
  N3: Часть1.D8, S1.IN1
  N4: Часть1.D7, S1.IN2
  N5: Часть1.D6_PWM, S1.ENA, S1.ENA-5V
  N6: Часть1.D4, S1.IN4
  N7: Часть1.D3_PWM, S1.ENB, S1.ENB-5V
  N8: Часть1.D2, S1.IN3
  N9: Часть2.SDA, GY2.pin5
  N10: Часть2.SCL, GY2.pin6
  N11: S1.M1-01, M2.pin_2
  N12: S1.M1-02, M2.pin_1
  N13: S1.M2-01, M1.pin_1
  N14: S1.M2-02, M1.pin_2

custom parts:
  MPU-6050 Board GY-521: Acelerometro y Giroscopio MPU-6050 Board GY-521
  H-Bridge with L298N: h-bridge
